// Logisim project alu.circ as structural Verilog: 4 circuits, main circuit ALU
module ALU (
  input  [3:0] OPCODE,
  input  [1:0] A,
  input  [1:0] B,
  output Z,
  output N,
  output [1:0] Y,
  output V,
  output C
);

  wire [1:0] au_1_y, lu_1_y, multiplexer_1_out, not_1_out;

  assign not_1_out = ~B;  // NOT_Gate not_1, 2 bits wide
  Multiplexer #(.width(2)) multiplexer_1 (.in0(B), .in1(not_1_out), .out(multiplexer_1_out), .sel(OPCODE[3]));
  AU au_1 (
    .A(A), .B(multiplexer_1_out), .F1(OPCODE[1]), .F2(OPCODE[2]), .F3(OPCODE[3]), .Y(au_1_y), .OVERFLOW(V),
    .COUT(C));
  LU lu_1 (.F1(OPCODE[1]), .F2(OPCODE[2]), .F3(OPCODE[3]), .A(A), .B(B), .Y(lu_1_y));
  Multiplexer #(.width(2)) multiplexer_2 (.in0(au_1_y), .in1(lu_1_y), .out({N, Y[0]}), .sel(OPCODE[0]));
  nor nor_1 (Z, Y[0], N);

  assign Y[1] = N;
endmodule

module LU (
  input  F1,
  input  F2,
  input  F3,
  input  [1:0] A,
  input  [1:0] B,
  output [1:0] Y
);

  wire [1:0] and_1_out, or_1_out, shifter_1_out, shifter_2_out, xor_1_out;

  Shifter #(.shift("lr"), .width(2)) shifter_1 (.in(A), .\dist (B[0]), .out(shifter_1_out));
  Shifter #(.width(2)) shifter_2 (.in(A), .\dist (B[0]), .out(shifter_2_out));
  assign and_1_out = A & B;  // AND_Gate and_1, 2 bits wide
  assign xor_1_out = A ^ B;  // XOR_Gate xor_1, 2 bits wide
  assign or_1_out = A | B;  // OR_Gate or_1, 2 bits wide
  Multiplexer #(.select(3), .width(2)) multiplexer_1 (
    .in0(shifter_1_out), .in1(shifter_2_out), .in2(and_1_out), .in3(xor_1_out), .in4(or_1_out), .in5(2'b00),
    .in6(2'b00), .in7(2'b00), .out(Y), .sel({F3, F2, F1}));
endmodule

module ADDER_SUBS (
  input  CIN,
  input  [1:0] A,
  input  [1:0] B,
  output [1:0] Y,
  output OVERFLOW,
  output COUT
);

  wire adder_1_cout;

  Adder #(.width(1)) adder_1 (.a(A[0]), .b(B[0]), .out(Y[0]), .cin(CIN), .cout(adder_1_cout));
  Adder #(.width(1)) adder_2 (.a(A[1]), .b(B[1]), .out(Y[1]), .cin(adder_1_cout), .cout(COUT));
  xor xor_1 (OVERFLOW, adder_1_cout, COUT);
endmodule

module AU (
  input  [1:0] A,
  input  [1:0] B,
  input  F1,
  input  F2,
  input  F3,
  output [1:0] Y,
  output OVERFLOW,
  output COUT
);

  wire adder_subs_1_overflow, or_1_out, xor_1_out;
  wire [1:0] adder_subs_1_y, divider_1_out, divider_1_rem, multiplier_1_cout, multiplier_1_out;

  Multiplier #(.width(2)) multiplier_1 (.a(A), .b(B), .out(multiplier_1_out), .cout(multiplier_1_cout));  // open: cin
  Divider #(.width(2)) divider_1 (.a(A), .b(B), .out(divider_1_out), .rem(divider_1_rem));  // open: upper
  ADDER_SUBS adder_subs_1 (.CIN(F3), .A(A), .B(B), .Y(adder_subs_1_y), .OVERFLOW(adder_subs_1_overflow), .COUT(COUT));
  or or_1 (or_1_out, multiplier_1_cout[0], multiplier_1_cout[1]);
  Multiplexer #(.select(2), .width(2)) multiplexer_1 (
    .in0(multiplier_1_out), .in1(divider_1_out), .in2(divider_1_rem), .in3(adder_subs_1_y), .out(Y),
    .sel({F2, F1}));
  xor xor_1 (xor_1_out, F1, F2);
  Multiplexer multiplexer_2 (.in0(or_1_out), .in1(adder_subs_1_overflow), .out(OVERFLOW), .sel(xor_1_out));

  // Notes on the sheet:
  //   MODULUS
endmodule
